# Fritzing sketch MicroPython-Mux (saved by Fritzing 0.9.5d)
circuit board: 8.46667cm x 5.64444cm
breadboards: 1

parts:
  ESP8266 = NodeMCU V1.0
  16_X_Mux = Analog Digital MUX Breakout
  R1 = Rotary Potentiometer (Large) [maximum_resistance=50kΩ package=THT]
  R2 = Rotary Potentiometer (Large) [maximum_resistance=50kΩ package=THT]
  R3 = Rotary Potentiometer (Large) [maximum_resistance=50kΩ package=THT]

nets:
  N1: ESP8266.D0, 16_X_Mux.S0
  N2: ESP8266.D1, 16_X_Mux.S1
  N3: ESP8266.D2, 16_X_Mux.S2
  N4: ESP8266.D3, 16_X_Mux.S3
  3V3: ESP8266.3V3, 16_X_Mux.VCC, R1.leg1, R2.leg1, R3.leg1
  GND: ESP8266.GND, 16_X_Mux.GND, 16_X_Mux.EN, R1.leg2, R2.leg2, R3.leg2
  N5: ESP8266.A0, 16_X_Mux.SIG
  N6: 16_X_Mux.C13, R3.wiper
  N7: 16_X_Mux.C14, R2.wiper
  N8: 16_X_Mux.C15, R1.wiper

custom parts:
  NodeMCU V1.0: ESP8266 based NodeMCU
